# Fritzing sketch Servo Control (saved by Fritzing 0.9.3b)
breadboards: 1

parts:
  U1 = NodeMCU V1.0
  Part1 = Breadboard Power Supply Board SMD
  R1 = Rotary Potentiometer (Small) [maximum_resistance=100kΩ package=THT]
  Squix1 = OLED 0.96" 128x64 I2C SSD1306
  J1 = Basic Servo

nets:
  N1: U1.D2, J1.pulse
  N2: U1.D3, Squix1.SCA
  N3: U1.D4, Squix1.SCL
  GND: U1.GND, Part1.GND, R1.leg2, Squix1.GND, J1.gnd
  N4: U1.A0, R1.wiper
  VCC: Part1.VCC, R1.leg1, Squix1.VCC, J1.vcc

notes:
  Power Grid: 5V
  Power Grid: 3.3V
  Power Input: 12V

custom parts:
  NodeMCU V1.0: ESP8266 based NodeMCU
